# Fritzing sketch nano-7segments (saved by Fritzing 0.9.3b)
breadboards: 1

parts:
  Part1 = Arduino Nano (Rev3.0)
  CLK = 7 Segment Display  # not connected
  DIO = 7 Segment Display  # not connected
  GND = 7 Segment Display  # not connected
  5V = 7 Segment Display  # not connected

nets:
  N1: Part1.D1/TX, Part1.GND
  N2: Part1.D2, Part1.D3, Part1.D6
