# Fritzing sketch nano-final (saved by Fritzing 0.9.3b)
breadboards: 1

parts:
  Part1 = Arduino Nano (Rev3.0)
  CLK = 7 Segment Display  # not connected
  DIO = 7 Segment Display  # not connected
  GND = 7 Segment Display  # not connected
  5V = 7 Segment Display  # not connected
  R1 = Resistor [tolerance=±5% resistance=220 package=THT]

nets:
  N1: Part1.D1/TX, Part1.GND, R1.Pin_0
  N2: Part1.D2, Part1.D3, Part1.D6
  N3: Part1.A1, R1.Pin_1
